# Fritzing sketch wise_you (saved by Fritzing 0.9.4)
breadboards: 1

parts:
  WeMos_D1_R1 = WeMos D1 R2
  DHT1 = DHT22 Humidity and Temperature Sensor
  부품1 = 24 NeoPixel Ring [part_number=1586]
  부품3 = Arduino Uno (Rev3) - ICSP
  R1 = Resistor [tolerance=±5% resistance=10k package="2010 [SMD]"]
  R2 = Resistor [tolerance=±5% resistance=20k package=THT]
  LCM1602_IIC2 = LCM1602 IIC [part_number="LCM1602 IIC" chip_label="LCM1602 IIC" package="DIP (Dual Inline) [THT]"]
  LCD2 = LCD screen
  LCM1602_IIC1 = LCM1602 IIC [part_number="LCM1602 IIC" chip_label="LCM1602 IIC" package="DIP (Dual Inline) [THT]"]
  LCD1 = LCD screen
  부품4 = Passive Buzzer  # not connected

nets:
  N1: WeMos_D1_R1.D0/RX, 부품3.D1/TX
  N2: WeMos_D1_R1.D1/TX, 부품3.D0/RX
  N3: WeMos_D1_R1.D14, LCM1602_IIC1.SDA
  N4: WeMos_D1_R1.D15, LCM1602_IIC1.SCL
  GND: WeMos_D1_R1.GND, DHT1.GND, 부품1.GND, 부품3.GND, 부품3.D3_PWM, LCM1602_IIC2.GND, LCM1602_IIC1.GND
  N5: WeMos_D1_R1.3.3V, R1.Pin_1, R2.Pin_0
  5V: WeMos_D1_R1.5V, LCM1602_IIC1.VCC
  VDD: DHT1.VDD, 부품1.VDD, 부품3.5V, R1.Pin_0, LCM1602_IIC2.VCC
  N6: DHT1.DATA, 부품3.D2
  N7: 부품1.IN, 부품3.D4
  N8: 부품3.A4/SDA, LCM1602_IIC2.SDA
  N9: 부품3.A5/SCL, LCM1602_IIC2.SCL
  VSS: LCM1602_IIC2.VSS, LCD2.VSS
  VDD_2: LCM1602_IIC2.VDD, LCD2.VDD
  N10: LCM1602_IIC2.V0, LCD2.V0
  N11: LCM1602_IIC2.RS, LCD2.RS
  N12: LCM1602_IIC2.RW, LCD2.R/W
  N13: LCM1602_IIC2.E, LCD2.E
  N14: LCM1602_IIC2.D0, LCD2.DB0
  N15: LCM1602_IIC2.D1, LCD2.DB1
  N16: LCM1602_IIC2.D2, LCD2.DB2
  N17: LCM1602_IIC2.D3, LCD2.DB3
  N18: LCM1602_IIC2.D4, LCD2.DB4
  N19: LCM1602_IIC2.D5, LCD2.DB5
  N20: LCM1602_IIC2.D6, LCD2.DB6
  N21: LCM1602_IIC2.D7, LCD2.DB7
  N22: LCM1602_IIC2.A, LCD2.LED+
  N23: LCM1602_IIC2.K, LCD2.LED-
  N24: LCM1602_IIC2.LED_A, LCM1602_IIC2.LED_B
  VSS_2: LCM1602_IIC1.VSS, LCD1.VSS
  VDD_3: LCM1602_IIC1.VDD, LCD1.VDD
  N25: LCM1602_IIC1.V0, LCD1.V0
  N26: LCM1602_IIC1.RS, LCD1.RS
  N27: LCM1602_IIC1.RW, LCD1.R/W
  N28: LCM1602_IIC1.E, LCD1.E
  N29: LCM1602_IIC1.D0, LCD1.DB0
  N30: LCM1602_IIC1.D1, LCD1.DB1
  N31: LCM1602_IIC1.D2, LCD1.DB2
  N32: LCM1602_IIC1.D3, LCD1.DB3
  N33: LCM1602_IIC1.D4, LCD1.DB4
  N34: LCM1602_IIC1.D5, LCD1.DB5
  N35: LCM1602_IIC1.D6, LCD1.DB6
  N36: LCM1602_IIC1.D7, LCD1.DB7
  N37: LCM1602_IIC1.A, LCD1.LED+
  N38: LCM1602_IIC1.K, LCD1.LED-
  N39: LCM1602_IIC1.LED_A, LCM1602_IIC1.LED_B

custom parts:
  WeMos D1 R2: The D1 R2 is a mini wifi board based on the ESP-8266EX.
  24 NeoPixel Ring: 24 ultra bright smart LED NeoPixels are arranged in a circle with 2.6" (66mm) outer diameter. The rings are 'chainable' - connect the output pin of one to the input pin of another. Use only one microcontroller pin to control as many as you can chain together! Each LED is addressable as the driver chip is inside the LED. Each one has ~18mA constant current drive so the color will be very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
  LCM1602 IIC: I2C-Module to use a 1602 or 2004 LCD on with the wire.h libory Serial LCD Modul
